# Fritzing sketch ESP32 Sensor Pack V1 diagram (saved by Fritzing 0.9.6b)
perfboards: 1

parts:
  M1 = DOIT Esp32 DevKit v1 (30 pins long, 11 pins width) [part_number=ESP32S-PIN30]
  positive_out = male alternating pin header, 3 pins [form="♂ (male)"]
  LED1 = LED - 5mm [color="Blue (470nm)" current=0.030 package="5 mm [THT]"]
  R2 = Vertical Resistor [tolerance=±5% resistance=220 package=THT]
  LED2 = LED - 5mm [color="Green (555nm)" current=0.030 package="5 mm [THT]"]
  WeDo_2_0_Spike_connection = male pin header, 6 pins [form="♂ (male)"]
  ESP32_breakout = male pin header, 8 pins [form="♂ (male)"]
  R3 = Vertical Resistor [tolerance=±5% resistance=220 package=THT]
  negative_out = male alternating pin header, 3 pins [form="♂ (male)"]

nets:
  N1: M1.3V3, positive_out.pin1, positive_out.pin3
  N2: M1.GND, LED2.cathode, WeDo_2_0_Spike_connection.pin4, negative_out.pin1, negative_out.pin3
  N3: M1.RX2, WeDo_2_0_Spike_connection.pin2
  N4: M1.TX2, LED1.anode, WeDo_2_0_Spike_connection.pin1
  N5: M1.D5, ESP32_breakout.pin8
  N6: M1.D18, ESP32_breakout.pin7
  N7: M1.D19, ESP32_breakout.pin6
  N8: M1.D21, ESP32_breakout.pin5
  N9: M1.RX0, ESP32_breakout.pin4
  N10: M1.TX0, ESP32_breakout.pin3
  N11: M1.D22, ESP32_breakout.pin2
  N12: M1.D23, ESP32_breakout.pin1
  N13: M1.VIN, WeDo_2_0_Spike_connection.pin6
  N14: R2.Pin_1, WeDo_2_0_Spike_connection.pin5
  N15: LED2.anode, R3.Pin_0, R3.Pin_1

notes:
  ESP 32 Sensor Pack V1, 2

custom parts:
  DOIT Esp32 DevKit v1 (30 pins long, 11 pins width): The DOIT Esp32 DevKit v1 is one of the development board created by DOIT to evaluate the ESP-WROOM-32 module. It is based on the ESP32 microcontroller that boasts Wifi, Bluetooth, Ethernet and Low Power support all in a single chip. (vanepp) made breadboard work, adjusted pin numbering and labels and reduced size of schematic and cleaned up pcb. This chip is 30pins long (2 x15) and 11 pins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
  Vertical Resistor: A generic resistor (0.25W)
